# Fritzing sketch Final sketch (saved by Fritzing 0.9.3b)
breadboards: 1

parts:
  Part1 = Arduino Uno (Rev3) - ICSP
  VCC1 = Battery block 9V
  Part2 = Bluetooth HC-05 Macho  # not connected
  J1 = Basic Servo
  J2 = Basic Servo
  J3 = Basic Servo
  U1 = TRANSCHIPTC5747 [package=camera_sfv24r-2st_2]

nets:
  N1: Part1.ICSP_MISO, U1.VALIDH
  N2: Part1.5V, U1.VALIDV
  N3: Part1.ICSP_SCK, U1.VCLK_OUT
  N4: Part1.ICSP_MOSI, U1.DVDD28
  N5: Part1.RESET, U1.PS1
  GND: Part1.GND, VCC1.-, J1.gnd, J2.gnd, J3.gnd, U1.SDIN
  N6: Part1.D3_PWM, J3.pulse
  N7: Part1.D4, J2.pulse
  N8: Part1.D5_PWM, J1.pulse
  VCC: VCC1.+, J1.vcc, J2.vcc, J3.vcc
